// Logisim project alu.circ as structural Verilog: 1 circuit, main circuit main
module main (
  input  A1,
  input  in_2,
  input  A2,
  input  B1,
  input  Subtract,
  input  B2,
  output C1,
  output C2,
  output out_9
);

  wire and_1_out, and_2_out, and_3_out, and_4_out, and_5_out, multiplexer_1_out, multiplexer_2_out,
       multiplexer_3_out, not_1_out, not_2_out, not_3_out, or_1_out, xor_1_out, xor_2_out, xor_3_out,
       xor_5_out;

  not not_1 (not_1_out, B1);
  not not_2 (not_2_out, 1'b1);
  Multiplexer #(.enable("false")) multiplexer_1 (.in0(B1), .in1(not_1_out), .out(multiplexer_1_out), .sel(Subtract));
  Multiplexer #(.enable("false")) multiplexer_2 (.in0(B2), .in1(not_3_out), .out(multiplexer_2_out), .sel(Subtract));
  not not_3 (not_3_out, B2);
  Multiplexer #(.enable("false")) multiplexer_3 (.in0(not_2_out), .in1(1'b1), .out(multiplexer_3_out), .sel(Subtract));
  xor xor_1 (xor_1_out, multiplexer_3_out, multiplexer_1_out);
  and and_1 (and_1_out, multiplexer_3_out, multiplexer_1_out);
  xor xor_2 (xor_2_out, A1, xor_1_out);
  xor xor_3 (xor_3_out, and_1_out, multiplexer_2_out);
  and and_2 (and_2_out, xor_2_out, in_2);
  and and_3 (and_3_out, A1, xor_1_out);
  xor xor_4 (C1, xor_2_out, in_2);
  or or_1 (or_1_out, and_2_out, and_3_out);
  xor xor_5 (xor_5_out, A2, xor_3_out);
  and and_4 (and_4_out, xor_5_out, or_1_out);
  and and_5 (and_5_out, A2, xor_3_out);
  or or_2 (out_9, and_4_out, and_5_out);
  xor xor_6 (C2, xor_5_out, or_1_out);

  // Notes on the sheet:
  //   S: 0 - add, 1 - subtract
  //   2bit 2s complement numbers to decimal
  //   00 : 0
  //   01 : 1
  //   10 : -2
  //   11 : -1
  //   Carry\Borrow
  //   B'1
  //   subtract numbers? - negate what you subtract and add
  //   negation: invert all bits and add one
  //   Inputs: A1, A2, B1, B2, Subtract? - operation, Carry\Borrow
  //   Output: C1, C2, Carry\Borrow
  //   B'2
  //   2 bit ALU that can add and subtract in complementary form and outputs carry
  //   Carry\Borrow (out)
endmodule
